// Logisim project ALU.circ as structural Verilog: 2 circuits, main circuit main
module main (
  input  [31:0] A,
  input  [31:0] B,
  input  [4:0] Shift,
  input  [3:0] Codop,
  input  CarryIn,
  output [31:0] S,
  output [3:0] Flags
);

  wire ADC_C, bitselector_1_out, bitselector_2_out, CMN_C, CMP_C, comparator_1_eq, not_1_out, not_6_out,
       overflow_1_sortie, overflow_2_sortie, overflow_3_sortie, overflow_4_sortie, SBC_C, subtractor_1_bout,
       subtractor_3_bout;
  wire [4:0] subtractor_6_out, subtractor_7_out;
  wire [31:0] adder_1_out, adder_3_out, adder_4_out, and_1_out, and_3_out, CMN_NZ, CMP_NZ, multiplexer_2_out,
       multiplier_1_out, not_2_out, not_3_out, not_7_out, not_8_out, or_1_out, shifter_1_out, shifter_2_out,
       shifter_3_out, shifter_4_out, subtractor_1_out, subtractor_2_out, subtractor_4_out, subtractor_5_out,
       TST_NZ, xor_1_out;

  not not_1 (not_1_out, CarryIn);
  assign not_2_out = ~A;  // NOT_Gate not_2, 32 bits wide
  assign not_3_out = ~A;  // NOT_Gate not_3, 32 bits wide
  assign and_1_out = A & B;  // AND_Gate and_1, 32 bits wide
  assign xor_1_out = A ^ B;  // XOR_Gate xor_1, 32 bits wide
  Shifter #(.width(32)) shifter_1 (.in(B), .\dist (Shift), .out(shifter_1_out));
  Shifter #(.shift("lr"), .width(32)) shifter_2 (.in(B), .\dist (Shift), .out(shifter_2_out));
  Shifter #(.shift("ar"), .width(32)) shifter_3 (.in(B), .\dist (Shift), .out(shifter_3_out));
  Adder #(.width(32)) adder_1 (.a(A), .b(B), .out(adder_1_out), .cin(CarryIn), .cout(ADC_C));
  Subtractor #(.width(32)) subtractor_1 (
    .a(B), .b(A), .out(subtractor_1_out), .bin(not_1_out), .bout(subtractor_1_bout));
  not not_4 (SBC_C, subtractor_1_bout);
  Shifter #(.shift("rr"), .width(32)) shifter_4 (.in(B), .\dist (Shift), .out(shifter_4_out));
  assign TST_NZ = A & B;  // AND_Gate and_2, 32 bits wide
  Subtractor #(.width(32)) subtractor_2 (.a({32{1'b0}}), .b(A), .out(subtractor_2_out));  // open: bin, bout
  Subtractor #(.width(32)) subtractor_3 (.a(B), .b(A), .out(CMP_NZ), .bout(subtractor_3_bout));  // open: bin
  not not_5 (CMP_C, subtractor_3_bout);
  Adder #(.width(32)) adder_2 (.a(B), .b(A), .out(CMN_NZ), .cout(CMN_C));  // open: cin
  assign or_1_out = A | B;  // OR_Gate or_1, 32 bits wide
  Multiplier #(.mode("twosComplement"), .width(32)) multiplier_1 (
    .a(A), .b(B), .out(multiplier_1_out));  // open: cin, cout
  assign and_3_out = not_2_out & B;  // AND_Gate and_3, 32 bits wide
  Multiplexer #(.select(4), .width(32)) multiplexer_1 (
    .in0(and_1_out), .in1(xor_1_out), .in2(shifter_1_out), .in3(shifter_2_out), .in4(shifter_3_out),
    .in5(adder_1_out), .in6(subtractor_1_out), .in7(shifter_4_out), .in8(B), .in9(subtractor_2_out),
    .in10(B), .in11(B), .in12(or_1_out), .in13(multiplier_1_out), .in14(and_3_out), .in15(not_3_out),
    .out(S), .sel(Codop));
  Adder #(.width(32)) adder_3 (.a(A), .b(B), .out(adder_3_out), .cin(CarryIn));  // open: cout
  not not_6 (not_6_out, CarryIn);
  Subtractor #(.width(32)) subtractor_4 (.a(B), .b(A), .out(subtractor_4_out), .bin(not_6_out));  // open: bout
  assign not_7_out = ~A;  // NOT_Gate not_7, 32 bits wide
  Subtractor #(.width(32)) subtractor_5 (.a(B), .b(A), .out(subtractor_5_out));  // open: bin, bout
  assign not_8_out = ~A;  // NOT_Gate not_8, 32 bits wide
  Adder #(.width(32)) adder_4 (.a(B), .b(A), .out(adder_4_out));  // open: cin, cout
  Subtractor #(.width(5)) subtractor_6 (.a({5{1'b0}}), .b(Shift), .out(subtractor_6_out));  // open: bin, bout
  BitSelector #(.width(32)) bitselector_1 (.in(B), .out(bitselector_1_out), .sel(subtractor_6_out));
  BitSelector #(.width(32)) bitselector_2 (.in(B), .out(bitselector_2_out), .sel(subtractor_7_out));
  Subtractor #(.width(5)) subtractor_7 (.a(Shift), .b(5'b00001), .out(subtractor_7_out));  // open: bin, bout
  Overflow overflow_1 (.A(A), .B(B), .Result(adder_3_out), .Sortie(overflow_1_sortie));
  Overflow overflow_2 (.A(not_7_out), .B(B), .Result(subtractor_4_out), .Sortie(overflow_2_sortie));
  Comparator #(.width(32)) comparator_1 (.a(A), .b(32'h80000000), .eq(comparator_1_eq));  // open: gt, lt
  Overflow overflow_3 (.A(not_8_out), .B(B), .Result(subtractor_5_out), .Sortie(overflow_3_sortie));
  Overflow overflow_4 (.A(A), .B(B), .Result(adder_4_out), .Sortie(overflow_4_sortie));
  Multiplexer #(.select(4), .width(32)) multiplexer_2 (
    .in0(S), .in1(S), .in2(S), .in3(S), .in4(S), .in5(S), .in6(S), .in7(S), .in8(TST_NZ), .in9(S),
    .in10(CMP_NZ), .in11(CMN_NZ), .in12(S), .in13(S), .in14(S), .in15(S), .out(multiplexer_2_out), .sel(Codop));
  Multiplexer #(.select(4)) multiplexer_3 (
    .in0(1'b0), .in1(1'b0), .in2(bitselector_1_out), .in3(bitselector_2_out), .in4(bitselector_2_out),
    .in5(ADC_C), .in6(SBC_C), .in7(Flags[3]), .in8(1'b0), .in9(1'b0), .in10(CMP_C), .in11(CMN_C),
    .in12(1'b0), .in13(1'b0), .in14(1'b0), .in15(1'b0), .out(Flags[1]), .sel(Codop));
  Comparator #(.width(32)) comparator_2 (
    .a(multiplexer_2_out), .b({32{1'b0}}), .eq(Flags[2]), .lt(Flags[3]));  // open: gt
  Multiplexer #(.select(4)) multiplexer_4 (
    .in0(1'b0), .in1(1'b0), .in2(1'b0), .in3(1'b0), .in4(1'b0), .in5(overflow_1_sortie),
    .in6(overflow_2_sortie), .in7(1'b0), .in8(1'b0), .in9(comparator_1_eq), .in10(overflow_3_sortie),
    .in11(overflow_4_sortie), .in12(1'b0), .in13(1'b0), .in14(1'b0), .in15(1'b0), .out(Flags[0]), .sel(Codop));

  // Other names for the same wires on the sheet: V = Flags[0]; C = Flags[1]; Z = Flags[2]; N = Flags[3]

  // Notes on the sheet:
  //   AND
  //   EOR
  //   LSL
  //   LSR
  //   ASR
  //   ADC
  //   SBC
  //   ROR
  //   TST
  //   RSB
  //   CMP
  //   CMN
  //   ORR
  //   MUL
  //   BIC
  //   MVN
endmodule

module Overflow (
  input  [31:0] Result,
  input  [31:0] A,
  input  [31:0] B,
  output Sortie
);

  wire and_1_out, and_2_out, not_1_out, not_2_out, not_3_out;

  not not_1 (not_1_out, Result[31]);
  not not_2 (not_2_out, A[31]);
  not not_3 (not_3_out, B[31]);
  and and_1 (and_1_out, not_1_out, A[31], B[31]);
  and and_2 (and_2_out, Result[31], not_2_out, not_3_out);
  or or_1 (Sortie, and_1_out, and_2_out);
endmodule
