// Logisim project Ctl_Conditional.circ as structural Verilog: 1 circuit, main circuit Conditional
module Conditional (
  input  Enable,
  input  [15:0] Instruction,
  input  Z,
  input  C,
  input  N,
  input  V,
  output [10:0] Offset,
  output Verified
);

  wire AL, AN, and_1_out, and_2_out, and_3_out, CC_LO, comparator_1_eq, comparator_2_eq, CS_HS, EQ, GE, GT,
       LE, LS, LT, MI, NE, not_1_out, not_2_out, not_3_out, not_4_out, not_5_out, or_1_out, PL, VC, VS;

  Demultiplexer #(.select(4)) demultiplexer_1 (
    .out0(EQ), .out1(NE), .out2(CS_HS), .out3(CC_LO), .out4(MI), .out5(PL), .out6(VS), .out7(VC),
    .out8(Verified), .out9(LS), .out10(GE), .out11(LT), .out12(GT), .out13(LE), .out14(AL), .out15(AN));  // open: in, sel
  not not_1 (not_1_out, Z);
  not not_2 (not_2_out, C);
  not not_3 (not_3_out, N);
  not not_4 (not_4_out, V);
  and and_1 (and_1_out, C, not_1_out);
  or or_1 (or_1_out, not_2_out, Z);
  Comparator #(.width(1)) comparator_1 (.a(N), .b(V), .eq(comparator_1_eq));  // open: gt, lt
  Comparator #(.width(1)) comparator_2 (.a(N), .b(V), .eq(comparator_2_eq));  // open: gt, lt
  not not_5 (not_5_out, comparator_2_eq);
  and and_2 (and_2_out, not_1_out, comparator_1_eq);
  and and_3 (and_3_out, Z, not_5_out);
  and and_4 (Verified, Z, EQ);
  and and_5 (Verified, not_1_out, NE);
  and and_6 (Verified, C, CS_HS);
  and and_7 (Verified, not_2_out, CC_LO);
  and and_8 (Verified, N, MI);
  and and_9 (Verified, not_3_out, PL);
  and and_10 (Verified, V, VS);
  and and_11 (Verified, not_4_out, VC);
  and and_12 (Verified, and_1_out, Verified);
  and and_13 (Verified, or_1_out, LS);
  and and_14 (Verified, comparator_1_eq, GE);
  and and_15 (Verified, and_2_out, LT);
  and and_16 (Verified, not_5_out, GT);
  and and_17 (Verified, and_3_out, LE);

  assign Instruction[10:8] = {3{Instruction[11]}};

  // Other names for the same wires on the sheet: HI = Verified
endmodule
