// Logisim project Ctl_Opcode_Decoder.circ as structural Verilog: 1 circuit, main circuit Opcode_Decoder
module Opcode_Decoder (
  input  [5:0] Opcode,
  output Shift,
  output Data_Processing,
  output Load_Store,
  output Conditional,
  output SP_Address
);

  wire comparator_1_eq, comparator_1_lt;

  Comparator #(.mode("unsigned"), .width(4)) comparator_1 (
    .a(Opcode[5:2]), .b(4'b0011), .eq(comparator_1_eq), .lt(comparator_1_lt));  // open: gt
  Comparator #(.mode("unsigned"), .width(6)) comparator_2 (
    .a(Opcode), .b(6'b010000), .eq(Data_Processing));  // open: gt, lt
  Comparator #(.mode("unsigned"), .width(4)) comparator_3 (
    .a(Opcode[5:2]), .b(4'b1001), .eq(Load_Store));  // open: gt, lt
  Comparator #(.mode("unsigned"), .width(4)) comparator_4 (
    .a(Opcode[5:2]), .b(4'b1101), .eq(Conditional));  // open: gt, lt
  Comparator #(.mode("unsigned"), .width(4)) comparator_5 (
    .a(Opcode[5:2]), .b(4'b1011), .eq(SP_Address));  // open: gt, lt
  or or_1 (Shift, comparator_1_eq, comparator_1_lt);

  // Notes on the sheet:
  //   Shift, add, sub, mov
  //   Load/Store
  //   SP Address
  //   Data Processing
  //   Conditional branch
endmodule
